# Fritzing sketch Mech-Agri Blueprint1 (saved by Fritzing 0.9.3b)
breadboards: 1

parts:
  A1 = 2 channel relay module [package=THT]
  A2 = 2 channel relay module [package=THT]
  VCC1 = Battery block 9V  # not connected
  Part1 = Arduino Uno (Rev3) - ICSP
  Capacitive_Soil_Moisture_Sensor1 = DFRobot Capacitive Soil Moisture Sensor V1.0 [part_number=SEN0193]
  Capacitive_Soil_Moisture_Sensor2 = DFRobot Capacitive Soil Moisture Sensor V1.0 [part_number=SEN0193]
  M1 = DC Motor
  M2 = DC Motor
  M3 = DC Motor
  J1 = Piezo Speaker
  DHT1 = DHT22 Humidity and Temperature Sensor
  Grove1 = Grove OLED 128x96
  MH-ET_LIVE_ESP32_DEVKIT1 = MH-ET LIVE ESP32 DEVKIT 38 pins
  R2 = Resistor [tolerance=±5% resistance=22 package=THT]
  R1 = Resistor [tolerance=±5% resistance=10 package="2010 [SMD]"]
  Capacitive_Soil_Moisture_Sensor3 = DFRobot Capacitive Soil Moisture Sensor V1.0 [part_number=SEN0193]

nets:
  N1: A1.pin_1, M2.pin_2
  N2: A1.pin_4, M3.pin_2
  5V: A1.pin_13, Part1.5V, Grove1.VCC
  GND: A1.pin_14, Part1.GND, Capacitive_Soil_Moisture_Sensor1.GND, Capacitive_Soil_Moisture_Sensor2.GND, DHT1.GND, Grove1.GND, MH-ET_LIVE_ESP32_DEVKIT1.GND, R2.Pin_1, Capacitive_Soil_Moisture_Sensor3.GND
  N3: A1.pin_15, Part1.D3_PWM
  N4: A1.pin_16, Part1.D4
  N5: A2.pin_4, M1.pin_2
  N6: A2.pin_15, Part1.D5_PWM
  N7: A2.pin_16, Part1.D6_PWM
  N8: Part1.A0, Capacitive_Soil_Moisture_Sensor1.A
  N9: Part1.A1, Capacitive_Soil_Moisture_Sensor3.A
  N10: Part1.A2, Capacitive_Soil_Moisture_Sensor2.A
  N11: Part1.A4/SDA, Grove1.SDA
  N12: Part1.A5/SCL, Grove1.SCL
  N13: Part1.D0/RX, MH-ET_LIVE_ESP32_DEVKIT1.IO17
  N14: Part1.D1/TX, R1.Pin_0
  N15: Part1.D2, DHT1.DATA
  VCC: Part1.3V3, Capacitive_Soil_Moisture_Sensor1.VCC, Capacitive_Soil_Moisture_Sensor2.VCC, DHT1.VDD, Capacitive_Soil_Moisture_Sensor3.VCC
  N16: M1.pin_1, M2.pin_1, M3.pin_1, J1.pin1

notes:
  1
  2
  3
  4
  10

custom parts:
  2 channel relay module: 2 channel Relay Module 5V 12V 24V High and Low Level Trigger Relay Control With Optocoupler Two Way relays DC 5 V 12 V 24 V Volt.
  DFRobot Capacitive Soil Moisture Sensor V1.0: DFRobot Capacitive Soil Moisture Sensor V1.0 This product measures soil moisture levels by capacitive sensing, rather than resistive sensing like other types of moisture sensor. It is made of a corrosion resistant material giving it a long service life. Insert it into soil and impress your friends with the real-time soil moisture data! The product includes an on-board voltage regulator which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
  MH-ET LIVE ESP32 DEVKIT 38 pins: http://mh.nodebb.com/topic/2/mh-et-live-esp32-devkit
